// Logisim project sap1.circ as structural Verilog
module main (
  input  in_1,
  input  in_2,
  input  in_3,
  input  in_4,
  input  in_5,
  input  in_6,
  input  in_7,
  input  in_8,
  input  in_9
);

  wire clock_1_out, clock_2_out, clock_3_out, clock_4_out;
  wire [3:0] cum2_1_marge_addr_out;
  wire [7:0] accumulator_1_acc_bus_out, accumulator_1_addsub_in, b_reg_1_b_accum_out,
       ram_hi16x8_1_data_out_bus, test_1_hello_hi_bus_out;

  Clock clock_1 (.out(clock_1_out));
  Clock clock_2 (.out(clock_2_out));
  CUM2 cum2_1 (
    .nLM(in_5), .CLK(clock_1_out), .bus_in(ram_hi16x8_1_data_out_bus), .marge_addr_out(cum2_1_marge_addr_out));
  ram_hi16x8 ram_hi16x8_1 (.mar_addr(cum2_1_marge_addr_out), .data_out_bus(ram_hi16x8_1_data_out_bus));  // open: nCE
  programcounter programcounter_1 (
    .C_P(in_1), .nCLK(clock_2_out), .nCLR(in_2), .E_P(in_3), .pc_bus_out(ram_hi16x8_1_data_out_bus));
  Clock clock_3 (.out(clock_3_out));
  Clock clock_4 (.out(clock_4_out));
  b_reg b_reg_1 (
    .nL_B(in_9), .CLK(clock_4_out), .b_bus_in(ram_hi16x8_1_data_out_bus), .b_accum_out(b_reg_1_b_accum_out));
  accumulator accumulator_1 (
    .nL_A(in_4), .CLK(clock_3_out), .E_A(in_6), .acc_bus_in(ram_hi16x8_1_data_out_bus),
    .acc_bus_out(accumulator_1_acc_bus_out), .addsub_in(accumulator_1_addsub_in));
  test test_1 (
    .A(accumulator_1_addsub_in), .B(b_reg_1_b_accum_out), .S_U(in_7), .E_U(in_8),
    .hello_hi_bus_out(test_1_hello_hi_bus_out));

  // Notes on the sheet:
  //   mar
  //   accumulator output
  //   add sum result
  //   b output
endmodule

// VHDL entity programcounter, as the project stores it:
library IEEE;
use IEEE.std_logic_1164.all;
use IEEE.numeric_std.all;

-- c_p = when active increment on falling edge
-- e_p = when active put program register onto bus
-- nclr = active low clr
-- nclk = active low clk

entity programcounter is -- WORKING
  port (
    C_P        : in std_logic;
    nCLK       : in std_logic;
    nCLR       : in std_logic;
    E_P        : in std_logic; -- will be used on top level implementation
    pc_bus_out : out std_logic_vector(7 downto 0)
  );
end;

architecture programcounter_rtl of programcounter is
  signal programcounter_reg : unsigned(3 downto 0) := (others => '0');
begin
  process (nCLK)
  begin
    if rising_edge(nCLK) then
      if nCLR = '0' then
        programcounter_reg <= (others => '0');
      elsif C_P = '1' then
        programcounter_reg <= programcounter_reg + 1;
      end if;
    end if;
  end process;
  pc_bus_out <= "0000" & std_logic_vector(programcounter_reg) when E_P = '1' else (others => 'Z');
end architecture;

// VHDL entity accumulator, as the project stores it:
library IEEE;
use IEEE.std_logic_1164.all;
use IEEE.numeric_std.all;
--nL_A = active low loading into accumulator
--e_a = active high loading from accumulator onto bus
-- CLK = active high clock

entity accumulator is --WORKING
  port (
    nL_A        : in std_logic;
    CLK         : in std_logic;
    E_A         : in std_logic;
    acc_bus_in  : in std_logic_vector(7 downto 0);
    acc_bus_out : out std_logic_vector(7 downto 0);
    addsub_in   : out std_logic_vector(7 downto 0)

  );
end;
architecture accumulator_rtl of accumulator is
  signal accumulator_reg : std_logic_vector(7 downto 0) := (others => '0');
begin
  process (CLK)
  begin
    if rising_edge(CLK) then
      if nL_A = '0' then
        accumulator_reg <= acc_bus_in;
      end if;
    end if;
  end process;

  acc_bus_out <= accumulator_reg when E_A = '1' else
    (others => 'Z');

  addsub_in <= accumulator_reg;
end architecture;

// VHDL entity b_reg, as the project stores it:
library IEEE;
use IEEE.std_logic_1164.all;
use IEEE.numeric_std.all;

entity b_reg is --WORKING
  port (
    nL_B        : in std_logic;
    CLK         : in std_logic;
    b_bus_in    : in std_logic_vector(7 downto 0);
    b_accum_out : out std_logic_vector(7 downto 0)

  );
end;

architecture b_rtl of b_reg is
  signal b_reg : std_logic_vector(7 downto 0) := (others => '0');
begin
  process (CLK)
  begin
    if rising_edge(CLK) then
      if nL_B = '0' then
        b_reg <= b_bus_in;
      end if;
    end if;
  end process;

  b_accum_out <= b_reg;
end architecture;

// VHDL entity ram_hi16x8, as the project stores it:
library IEEE;
use IEEE.std_logic_1164.all;
use IEEE.numeric_std.all;

entity ram_hi16x8 is
  port (
    mar_addr     : in std_logic_vector (3 downto 0);
    nCE           : in std_logic;
    data_out_bus : out std_logic_vector(7 downto 0) 
  );
end;

architecture rtl_ram_hi of ram_hi16x8 is
  type ram_hi_type is array (0 to 15) of STD_LOGIC_VECTOR(7 downto 0);
  signal ram_hi : ram_hi_type := (
    0 => "00000101", -- LDA 5
    1 => "00010110", -- ADD 6
    2 => "11100000", -- output
    5 => "00000101",
    6 => "00000101",
    others => (others => '0')
  );
begin
  data_out_bus <= ram_hi(to_integer(unsigned(mar_addr))) when nCE='0' else (others => 'Z');
  

end architecture;

// VHDL entity test, as the project stores it:
library IEEE;
use IEEE.std_logic_1164.all;
use IEEE.numeric_std.all;

entity test is
  port (
    A                : in std_logic_vector(7 downto 0);
    B                : in std_logic_vector(7 downto 0);
    S_U              : in std_logic; -- 0 = ADD, 1 = SUB
    E_U              : in std_logic; -- enable to bus
    hello_hi_bus_out : out std_logic_vector(7 downto 0)
  );
end;

architecture hello_hi_rtl of test is

  signal result : std_logic_vector(7 downto 0);
begin

  process (A, B, S_U)
  begin
    if S_U = '0' then
      result <= std_logic_vector(unsigned(A) + unsigned(B));
    else
      result <= std_logic_vector(unsigned(A) - unsigned(B));
    end if;
  end process;

  hello_hi_bus_out <= result when E_U = '1' else
    (others => 'Z');

end;

// VHDL entity CUM2, as the project stores it:
library IEEE;
use IEEE.std_logic_1164.all;
use IEEE.numeric_std.all;

entity CUM2 is
  port (
    nLM          : in std_logic;
    CLK          : in std_logic;
    bus_in       : in std_logic_vector(7 downto 0);
    marge_addr_out : out std_logic_vector(3 downto 0)
  );
end;

architecture marge_rtl of CUM2 is
  signal marge_reg : std_logic_vector(3 downto 0) := (others => '0');
begin
  process (CLK)
  begin
    if rising_edge(CLK) then
      if nLM = '0' then
        marge_reg <= bus_in(3 downto 0); -- only lower 4 bits
      end if;
    end if;
  end process;

  marge_addr_out <= marge_reg;
end architecture;
